# Fritzing sketch scheme (saved by Fritzing 0.9.4)

parts:
  RP_Pico = Raspberry Pi Pico
  R1_3kΩ = Resistor [tolerance=±5% resistance=3k package=THT]
  R2_3kΩ = Resistor [tolerance=±5% resistance=3k package=THT]
  R3_3kΩ = Resistor [tolerance=±5% resistance=3k package=THT]
  D1 = Schottky Diode [part_number=1N5817 package="300 mil [THT]"]
  D2 = Schottky Diode [part_number=1N5817 package="300 mil [THT]"]
  D3 = Schottky Diode [part_number=1N5817 package="300 mil [THT]"]
  J1 = female pin header, 5 pins [form="♀ (female)"]
  D4 = Schottky Diode [part_number=1N5817 package="300 mil [THT]"]

nets:
  N1: RP_Pico.pin_3, RP_Pico.pin_42, J1.pin1
  N2: RP_Pico.pin_4, R3_3kΩ.Pin_0, D1.anode
  N3: RP_Pico.pin_5, R2_3kΩ.Pin_0, D2.anode
  N4: RP_Pico.pin_6, R1_3kΩ.Pin_0, D3.anode
  N5: RP_Pico.pin_36, D1.cathode, D2.cathode, D3.cathode
  N6: RP_Pico.pin_39, D4.cathode
  N7: R1_3kΩ.Pin_1, J1.pin4
  N8: R2_3kΩ.Pin_1, J1.pin3
  N9: R3_3kΩ.Pin_1, J1.pin2
  N10: J1.pin5, D4.anode

notes:
  VBUS - VCC
  GP4 - CLK
  GP3 - DATA
  GP2 - SEL
  GND - GND

custom parts:
  Raspberry Pi Pico: Raspberry Pi Pico. Based around the RP2040 microcontroller the Pico is a low cost microcontroller device bringing Raspberry Pi quality, cost, and easy of use to the microcontroller space. Jan 2021, Split part in to two versions: tht (this one) and SMD. This one will drill holes for a .1 in header in pcb to allow plugging in the module as well as providing pads to solder the module to the top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
